# Fritzing sketch kuehlschrank_sicherheit (saved by Fritzing 0.9.3b)
breadboards: 1

parts:
  Part1 = Arduino Uno (Rev3)
  Part2 = Arduino Uno (Rev3)
  microSD1 = MicroSD Card Module
  CAMERA1 = TTL Serial JPEG Camera
  Part3 = LED Tactile Button Breakout v10 [part_number=BOB-10467]
  Part4 = RFID-RC522 [part_number=101218]
  R1 = Resistor [tolerance=±5% resistance=220 package=THT]
  R2 = Resistor [tolerance=±5% resistance=220 package=THT]

nets:
  N1: Part1.A4/SDA, Part2.A4/SDA
  N2: Part1.A5/SCL, Part2.A5/SCL
  N3: Part1.D10_PWM/SS, microSD1.CS
  N4: Part1.D11_PWM/MOSI, microSD1.MOSI
  N5: Part1.D12/MISO, microSD1.MISO
  N6: Part1.D13/SCK, microSD1.SCK
  GND: Part1.GND, Part2.GND, microSD1.GND, CAMERA1.GND, Part3.2, Part4.GND, R1.Pin_1
  N7: Part1.D2, CAMERA1.RX
  N8: Part1.D3_PWM, R2.Pin_1
  5V: Part1.5V, microSD1.VCC, CAMERA1.5V
  N9: Part2.D9_PWM, Part4.RST
  N10: Part2.D10_PWM/SS, Part4.SDA
  N11: Part2.D11_PWM/MOSI, Part4.MOSI
  N12: Part2.D12/MISO, Part4.MISO
  N13: Part2.D13/SCK, Part4.SCK
  N14: Part2.D3_PWM, Part3.3
  3V3: Part2.3V3, Part4.3.3V
  N15: Part2.5V, Part3.1
  N16: CAMERA1.TX, R1.Pin_0, R2.Pin_0

custom parts:
  TTL Serial JPEG Camera: TTL Serial JPEG Camera with NTSC Out
